# Fritzing sketch HC-06 (saved by Fritzing 0.9.3b)

parts:
  ARDUINO1 = Arduino Micro
  BT1 = Bluetooth HC-06d [package=THT]
  R2 = Resistor [tolerance=±5% resistance=20k package="0603 [SMD]"]
  R1 = Resistor [tolerance=±5% resistance=10k package="0603 [SMD]"]

nets:
  N1: ARDUINO1.D10, BT1.TXD
  N2: ARDUINO1.D11, R1.Pin_0
  5V: ARDUINO1.5V, BT1.VCC
  GND: ARDUINO1.GND, BT1.GND
  N3: R2.Pin_0, R1.Pin_1

notes:
  10kΩ
  20kΩ

custom parts:
  Arduino Micro: Arduino Micro Microcontroller
  Bluetooth HC-06d: Bluetooth HC-06 - face down, pins down 16.5mm x 37.5mm PCB
