# Fritzing sketch HC-SR04 (saved by Fritzing 0.9.3b)

parts:
  ARDUINO1 = Arduino Micro
  HC-SR04_Sensor_1 = HC-SR04 Ultrasonic Distance Sensor

nets:
  GND: ARDUINO1.GND, HC-SR04_Sensor_1.GND
  N1: ARDUINO1.D7, HC-SR04_Sensor_1.ECHO
  N2: ARDUINO1.D8, HC-SR04_Sensor_1.TRIG
  5V: ARDUINO1.5V, HC-SR04_Sensor_1.VCC

custom parts:
  Arduino Micro: Arduino Micro Microcontroller
