# Fritzing sketch LED (saved by Fritzing 0.9.3b)

parts:
  ARDUINO1 = Arduino Micro
  LED2 = smd LED [color="Yellow (595nm)" package="1206 [SMD]"]
  R1 = Resistor [tolerance=±5% resistance=220 package="1206 [SMD]"]

nets:
  N1: ARDUINO1.GND, LED2.cathode
  N2: ARDUINO1.D13, R1.Pin_1
  N3: LED2.anode, R1.Pin_0

notes:
  220Ω

custom parts:
  Arduino Micro: Arduino Micro Microcontroller
