# Fritzing sketch MFRC522 (saved by Fritzing 0.9.3b)

parts:
  ARDUINO1 = Arduino Micro
  Part1 = RFID-RC522-v2

nets:
  N1: ARDUINO1.MOSI, Part1.MOSI
  N2: ARDUINO1.SS, Part1.SDA
  GND: ARDUINO1.GND, Part1.GND
  N3: ARDUINO1.D5, Part1.RST
  N4: ARDUINO1.3V3, Part1.3_3V
  N5: ARDUINO1.MISO, Part1.MISO
  N6: ARDUINO1.SCK, Part1.SCK

custom parts:
  Arduino Micro: Arduino Micro Microcontroller
  RFID-RC522-v2: A simple China made RFID-RC522 Reader; do check the pin labels, as this is a MFRC522 based clone.
