# Fritzing sketch OLED (saved by Fritzing 0.9.3b)

parts:
  ARDUINO1 = Arduino Micro
  OLED1 = OLED Mono 0.56 inch blue or white

nets:
  GND: ARDUINO1.GND, OLED1.GND
  N1: ARDUINO1.D2, OLED1.SDA
  N2: ARDUINO1.D3, OLED1.SCL
  5V: ARDUINO1.5V, OLED1.VCC

custom parts:
  Arduino Micro: Arduino Micro Microcontroller
  OLED Mono 0.56 inch blue or white: OLED, I2C 3.3V - 5V Blue and White text versions
