# Fritzing sketch POTENTIOMETER (saved by Fritzing 0.9.3b)

parts:
  ARDUINO1 = Arduino Micro
  U1 = POT_SWITCH [package=pot_pth_switch]

nets:
  N1: ARDUINO1.GND, U1.G$1_A
  N2: ARDUINO1.A0, U1.G$2_1
  N3: ARDUINO1.5V, U1.G$2_2

custom parts:
  Arduino Micro: Arduino Micro Microcontroller
